# Fritzing sketch Schematics (saved by Fritzing 0.9.2b)
breadboards: 1

parts:
  Onderdeel1 = Arduino Pro Mini v13
  DHT1 = DHT22 Humidity and Temperature Sensor
  OLED1 = 128x64 Monochrom OLED Display with SPI Control
  Q1 = Basic FET N-Channel [package="TO220 [THT]"]
  JP1 = Header 4 [package=jst-4-pth]
  D1 = Zener Diode [part_number=1N4732A breakdown_voltage=3.6V package="300 mil [THT]"]
  R1 = Resistor [tolerance=±5% resistance=4.7k package=THT]
  J1 = Power Jack [package=power_jack_pth]

nets:
  N1: Onderdeel1.A4, OLED1.Data
  N2: Onderdeel1.A5, OLED1.Clock
  N3: Onderdeel1.RAW, JP1.2, D1.cathode, J1.PWR
  GND: Onderdeel1.GND, DHT1.GND, OLED1.GND, Q1.source, J1.GND
  VCC: Onderdeel1.VCC, DHT1.VDD, OLED1.Vin, R1.Pin_1
  N4: Onderdeel1.D11_PWM/MOSI, DHT1.DATA, R1.Pin_0
  N5: Onderdeel1.D10_PWM/SS, Q1.gate
  N6: Onderdeel1.D9_PWM, JP1.3
  N7: Onderdeel1.D3_PWM, JP1.4
  N8: Q1.drain, JP1.1, D1.anode

notes:
  COOLER FAN:
  CONTROL = BLUE
  SENSE = GREEN
  +12v = YELLOW
  GND = BLACK
  12V DC Power
